# Fritzing sketch rpi3_schematics (saved by Fritzing 0.9.3b)
circuit board: 8.46667cm x 5.64444cm
breadboards: 1

parts:
  S1 = Pushbutton [package="[THT]"]
  R2 = Resistor [tolerance=±5% resistance=220 package="0402 [SMD]"]
  LED1 = smd LED [color="Red (633nm)" package="1206 [SMD]"]
  Raspberry_Pi_1 = Raspberry Pi 3 [part_number=RPI-3-V1.2]
  R1 = Resistor [tolerance=±5% resistance=10k package="0402 [SMD]"]
  LED2 = smd LED [color="Green (555nm)" package="1206 [SMD]"]
  R3 = Resistor [tolerance=±5% resistance=220 package="0402 [SMD]"]
  S2 = Pushbutton [package="[THT]"]
  R4 = Resistor [tolerance=±5% resistance=10k package="0402 [SMD]"]

nets:
  N1: S1.Pin_1, S1.Pin_2, LED1.cathode, Raspberry_Pi_1.GND, LED2.cathode, S2.Pin_1, S2.Pin_2
  N2: S1.Pin_3, S1.Pin_4, Raspberry_Pi_1.GPIO21, R1.Pin_1
  N3: R2.Pin_0, Raspberry_Pi_1.GPIO6
  N4: R2.Pin_1, LED1.anode
  N5: Raspberry_Pi_1.GPIO5, R3.Pin_0
  N6: Raspberry_Pi_1.GPIO20, S2.Pin_3, S2.Pin_4, R4.Pin_1
  N7: Raspberry_Pi_1.5V, R1.Pin_0, R4.Pin_0
  N8: LED2.anode, R3.Pin_1
